# Fritzing sketch rpi_birdbox_camera (saved by Fritzing 0.8.7b)

parts:
  Raspberry_Pi_1 = Raspberry Pi 3 [part_number=RPI-3-V1.2]
  R1 = Resistor [tolerance=±5% resistance=220 package=THT]
  LED1 = LED - 5mm [color="Infrared (850nm)" package="5 mm [THT]"]

nets:
  N1: Raspberry_Pi_1.3v3, R1.Pin_0
  N2: Raspberry_Pi_1.GND, LED1.cathode
  N3: R1.Pin_1, LED1.anode

notes:
  Insert camera cable here.
